// Logisim project t1.circ as structural Verilog: 9 circuits, main circuit main
module main (
  input  Sub,
  input  [15:0] in_2,
  input  [15:0] in_3,
  output [15:0] out_4,
  output out_5
);

  wire [15:0] multiplexer_1_out, not_1_out;

  assign not_1_out = ~in_3;  // NOT_Gate not_1, 16 bits wide
  Multiplexer #(.width(16), .enable("false")) multiplexer_1 (
    .in0(in_3), .in1(not_1_out), .out(multiplexer_1_out), .sel(Sub));
  CLA_16bit cla_16bit_1 (
    .Cin(Sub), .A(in_2), .B(multiplexer_1_out), .S(out_4), .overflow(out_5));  // open: PG, GG, Cout
endmodule

module mult_8bit (
  input  [7:0] in_1,
  input  [7:0] in_2
);

  shiftLR_16bit shiftlr_16bit_1 ();  // open: Vout, LR, Vin
endmodule

module BCDadder_8bit (
  input  [7:0] A,
  input  [7:0] B,
  output [7:0] S,
  output Cout
);

  wire bin2bcd_4bit_1_cout;
  wire [3:0] cla_4bit_1_s, cla_4bit_2_s;

  CLA_4bit cla_4bit_1 (.Cin(1'b0), .A(A[3:0]), .B(B[3:0]), .S(cla_4bit_1_s));  // open: PG, GG, Cout, overflow
  Bin2BCD_4bit bin2bcd_4bit_1 (.Bin(cla_4bit_1_s), .BCD(S[3:0]), .Cout(bin2bcd_4bit_1_cout));
  CLA_4bit cla_4bit_2 (
    .Cin(bin2bcd_4bit_1_cout), .A(A[7:4]), .B(B[7:4]), .S(cla_4bit_2_s));  // open: PG, GG, Cout, overflow
  Bin2BCD_4bit bin2bcd_4bit_2 (.Bin(cla_4bit_2_s), .BCD(S[7:4]), .Cout(Cout));

  // Other names for the same wires on the sheet: A0[3:0] = A[3:0]; A1[3:0] = A[7:4]; B0[3:0] = B[3:0];
  //   B1[3:0] = B[7:4]
endmodule

module Bin2BCD_4bit (
  input  [3:0] Bin,
  output [3:0] BCD,
  output Cout
);

  wire or_1_out;
  wire [3:0] cla_4bit_1_s;

  or or_1 (or_1_out, Bin[1], Bin[2]);
  and and_1 (Cout, or_1_out, Bin[3]);
  CLA_4bit cla_4bit_1 (.Cin(1'b0), .A(Bin), .B(4'b0110), .S(cla_4bit_1_s));  // open: PG, GG, Cout, overflow
  Multiplexer #(.width(4), .enable("false")) multiplexer_1 (.in0(Bin), .in1(cla_4bit_1_s), .out(BCD), .sel(Cout));
endmodule

module CLA_16bit (
  input  Cin,
  input  [15:0] A,
  input  [15:0] B,
  output [15:0] S,
  output PG,
  output GG,
  output Cout,
  output overflow
);

  wire C1, C2, C3, G0, G1, G2, G3, P0, P1, P2, P3;

  CLA_4bit cla_4bit_1 (.Cin(Cin), .A(A[3:0]), .B(B[3:0]), .S(S[3:0]), .PG(P0), .GG(G0));  // open: Cout, overflow
  CLA_4bit cla_4bit_2 (.Cin(C1), .A(A[7:4]), .B(B[7:4]), .S(S[7:4]), .PG(P1), .GG(G1));  // open: Cout, overflow
  CLA_4bit cla_4bit_3 (.Cin(C2), .A(A[11:8]), .B(B[11:8]), .S(S[11:8]), .PG(P2), .GG(G2));  // open: Cout, overflow
  CLA_4bit cla_4bit_4 (.Cin(C3), .A(A[15:12]), .B(B[15:12]), .S(S[15:12]), .PG(P3), .GG(G3));  // open: Cout, overflow
  CLU_4in clu_4in_1 (
    .C0(Cin), .P0(P0), .P1(P1), .P2(P2), .P3(P3), .G0(G0), .G1(G1), .G2(G2), .G3(G3), .C1(C1), .C2(C2),
    .C3(C3), .C4(Cout), .PG(PG), .GG(GG), .overflow(overflow));

  // Other names for the same wires on the sheet: A0[3:0] = A[3:0]; A1[3:0] = A[7:4]; A2[3:0] = A[11:8];
  //   A3[3:0] = A[15:12]; B0[3:0] = B[3:0]; B1[3:0] = B[7:4]; B2[3:0] = B[11:8]; B3[3:0] = B[15:12]; C4 = Cout;
  //   S0[3:0] = S[3:0]; S1[3:0] = S[7:4]; S2[3:0] = S[11:8]; S3[3:0] = S[15:12]
endmodule

module CLA_4bit (
  input  Cin,
  input  [3:0] A,
  input  [3:0] B,
  output [3:0] S,
  output PG,
  output GG,
  output Cout,
  output overflow
);

  wire C1, C2, C3, G0, G1, G2, G3, P0, P1, P2, P3;

  adder_1bit adder_1bit_1 (.C(Cin), .A(A[0]), .B(B[0]), .S(S[0]), .P(P0), .G(G0));
  adder_1bit adder_1bit_2 (.C(C1), .A(A[1]), .B(B[1]), .S(S[1]), .P(P1), .G(G1));
  adder_1bit adder_1bit_3 (.C(C2), .A(A[2]), .B(B[2]), .S(S[2]), .P(P2), .G(G2));
  adder_1bit adder_1bit_4 (.C(C3), .A(A[3]), .B(B[3]), .S(S[3]), .P(P3), .G(G3));
  CLU_4in clu_4in_1 (
    .C0(Cin), .P0(P0), .P1(P1), .P2(P2), .P3(P3), .G0(G0), .G1(G1), .G2(G2), .G3(G3), .C1(C1), .C2(C2),
    .C3(C3), .C4(Cout), .PG(PG), .GG(GG), .overflow(overflow));

  // Other names for the same wires on the sheet: C4 = Cout
endmodule

module CLU_4in (
  input  C0,
  input  P0,
  input  P1,
  input  P2,
  input  P3,
  input  G0,
  input  G1,
  input  G2,
  input  G3,
  output C1,
  output C2,
  output C3,
  output C4,
  output PG,
  output GG,
  output overflow
);

  wire and_1_out, and_2_out, and_3_out, and_4_out, and_5_out, and_6_out, and_8_out, and_9_out, and_10_out,
       and_11_out;

  and and_1 (and_1_out, C0, P0);
  or or_1 (C1, and_1_out, G0);
  and and_2 (and_2_out, C0, P0, P1);
  and and_3 (and_3_out, G0, P1);
  or or_2 (C2, and_2_out, and_3_out, G1);
  and and_4 (and_4_out, C0, P0, P1, P2);
  and and_5 (and_5_out, G0, P1, P2);
  and and_6 (and_6_out, G1, P2);
  or or_3 (C3, and_4_out, and_5_out, and_6_out, G2);
  and and_7 (PG, P0, P1, P2, P3);
  and and_8 (and_8_out, G0, P1, P2, P3);
  and and_9 (and_9_out, G1, P2, P3);
  and and_10 (and_10_out, G2, P3);
  xor xor_1 (overflow, C4, C3);
  or or_4 (GG, and_8_out, and_9_out, and_10_out, G3);
  and and_11 (and_11_out, C0, PG);
  or or_5 (C4, and_11_out, GG);

  // Notes on the sheet:
  //   Carry 1
  //   Carry 2
  //   Carry 3
endmodule

module adder_1bit (
  input  C,
  input  A,
  input  B,
  output S,
  output P,
  output G
);

  xor xor_1 (P, A, B);
  xor xor_2 (S, C, P);
  and and_1 (G, A, B);
endmodule

module shiftLR_16bit (
  input  [15:0] Vin,
  input  LR,
  output [15:0] Vout
);

  Multiplexer #(.enable("false")) multiplexer_1 (.in0(Vin[14]), .in1(1'b0), .out(Vout[15]), .sel(LR));
  Multiplexer #(.enable("false")) multiplexer_2 (.in0(Vin[13]), .in1(Vin[15]), .out(Vout[14]), .sel(LR));
  Multiplexer #(.enable("false")) multiplexer_3 (.in0(Vin[12]), .in1(Vin[14]), .out(Vout[13]), .sel(LR));
  Multiplexer #(.enable("false")) multiplexer_4 (.in0(Vin[10]), .in1(Vin[12]), .out(Vout[11]), .sel(LR));
  Multiplexer #(.enable("false")) multiplexer_5 (.in0(Vin[11]), .in1(Vin[13]), .out(Vout[12]), .sel(LR));
  Multiplexer #(.enable("false")) multiplexer_6 (.in0(Vin[9]), .in1(Vin[11]), .out(Vout[10]), .sel(LR));
  Multiplexer #(.enable("false")) multiplexer_7 (.in0(Vin[8]), .in1(Vin[10]), .out(Vout[9]), .sel(LR));
  Multiplexer #(.enable("false")) multiplexer_8 (.in0(Vin[7]), .in1(Vin[9]), .out(Vout[8]), .sel(LR));
  Multiplexer #(.enable("false")) multiplexer_9 (.in0(Vin[5]), .in1(Vin[7]), .out(Vout[6]), .sel(LR));
  Multiplexer #(.enable("false")) multiplexer_10 (.in0(Vin[6]), .in1(Vin[8]), .out(Vout[7]), .sel(LR));
  Multiplexer #(.enable("false")) multiplexer_11 (.in0(Vin[4]), .in1(Vin[6]), .out(Vout[5]), .sel(LR));
  Multiplexer #(.enable("false")) multiplexer_12 (.in0(Vin[2]), .in1(Vin[4]), .out(Vout[3]), .sel(LR));
  Multiplexer #(.enable("false")) multiplexer_13 (.in0(Vin[3]), .in1(Vin[5]), .out(Vout[4]), .sel(LR));
  Multiplexer #(.enable("false")) multiplexer_14 (.in0(Vin[0]), .in1(Vin[2]), .out(Vout[1]), .sel(LR));
  Multiplexer #(.enable("false")) multiplexer_15 (.in0(Vin[1]), .in1(Vin[3]), .out(Vout[2]), .sel(LR));
  Multiplexer #(.enable("false")) multiplexer_16 (.in0(1'b0), .in1(Vin[1]), .out(Vout[0]), .sel(LR));

  // Other names for the same wires on the sheet: dir = LR; V0 = Vin[0]; V1 = Vin[1]; V2 = Vin[2]; V3 = Vin[3];
  //   V4 = Vin[4]; V5 = Vin[5]; V6 = Vin[6]; V7 = Vin[7]; V8 = Vin[8]; V9 = Vin[9]; V10 = Vin[10]; V11 = Vin[11];
  //   V12 = Vin[12]; V13 = Vin[13]; V14 = Vin[14]; V15 = Vin[15]
endmodule
