// Logisim project t2.circ as structural Verilog: 6 circuits, main circuit main
module main (
  input  msg_bit,
  input  [31:0] polyn,
  input  load_polyn,
  input  clk,
  input  first_bit,
  input  R,
  output [31:0] out_7
);

  wire and_1_out, d_ff_1_q, nor_1_out;
  wire [31:0] count_32bit_1_out_3, register_1_q;

  Register #(.width(32)) register_1 (.D(polyn), .en(1'b1), .clk(load_polyn), .Q(register_1_q), .clr(1'b0));
  D_Flip_Flop d_ff_1 (.D(1'b1), .clk(and_1_out), .Q(d_ff_1_q), .reset(R));  // open: Qn, preset
  and and_1 (and_1_out, clk, first_bit);
  nor nor_1 (nor_1_out, first_bit, d_ff_1_q);
  count_32bit count_32bit_1 (.clk(clk), .R(nor_1_out), .out_3(count_32bit_1_out_3));  // open: count_out
  equals equals_1 (.A(count_32bit_1_out_3), .B(32'h1f4));  // open: v_out
  // calc calc_1: pin names not known; wires that end beside it: msg_bit, register_1_q, 1'b1, clk, nor_1_out, out_7

  // Notes on the sheet:
  //   polinomio
  //   500
endmodule

module bit_push (
  input  \bit ,
  input  [31:0] value,
  output [31:0] value_out
);


  assign value_out = {value[30:0], \bit };
endmodule

module calc (
  input  [31:0] G,
  input  \bit ,
  input  WE,
  input  R,
  input  clk,
  output [31:0] out_6,
  output [31:0] D
);

  wire and_1_out, d_ff_1_q;
  wire [31:0] multiplexer_1_out, xor_1_out;

  Register #(.width(32)) register_1 (.D(out_6), .en(WE), .clk(clk), .Q(D), .clr(R));
  and and_1 (and_1_out, clk, WE);
  D_Flip_Flop d_ff_1 (.D(D[31]), .clk(and_1_out), .Q(d_ff_1_q), .reset(R));  // open: Qn, preset
  assign xor_1_out = G ^ D;  // XOR_Gate xor_1, 32 bits wide
  Multiplexer #(.width(32), .enable("false")) multiplexer_1 (
    .in0(D), .in1(xor_1_out), .out(multiplexer_1_out), .sel(d_ff_1_q));
  bit_push bit_push_1 (.\bit (\bit ), .value(multiplexer_1_out), .value_out(out_6));

  // Other names for the same wires on the sheet: rst = R
endmodule

module count_8bit (
  input  clk,
  input  R,
  output [7:0] value,
  output count_out
);

  wire t_ff_1_qn, t_ff_2_qn, t_ff_3_qn, t_ff_4_qn, t_ff_5_qn, t_ff_6_qn, t_ff_7_qn;

  T_Flip_Flop t_ff_1 (.T(1'b1), .clk(clk), .Q(value[0]), .Qn(t_ff_1_qn), .reset(R));  // open: preset
  T_Flip_Flop t_ff_2 (.T(1'b1), .clk(t_ff_1_qn), .Q(value[1]), .Qn(t_ff_2_qn), .reset(R));  // open: preset
  T_Flip_Flop t_ff_3 (.T(1'b1), .clk(t_ff_2_qn), .Q(value[2]), .Qn(t_ff_3_qn), .reset(R));  // open: preset
  T_Flip_Flop t_ff_4 (.T(1'b1), .clk(t_ff_3_qn), .Q(value[3]), .Qn(t_ff_4_qn), .reset(R));  // open: preset
  T_Flip_Flop t_ff_5 (.T(1'b1), .clk(t_ff_4_qn), .Q(value[4]), .Qn(t_ff_5_qn), .reset(R));  // open: preset
  T_Flip_Flop t_ff_6 (.T(1'b1), .clk(t_ff_5_qn), .Q(value[5]), .Qn(t_ff_6_qn), .reset(R));  // open: preset
  T_Flip_Flop t_ff_7 (.T(1'b1), .clk(t_ff_6_qn), .Q(value[6]), .Qn(t_ff_7_qn), .reset(R));  // open: preset
  T_Flip_Flop t_ff_8 (.T(1'b1), .clk(t_ff_7_qn), .Q(value[7]), .Qn(count_out), .reset(R));  // open: preset
endmodule

module count_32bit (
  input  clk,
  input  R,
  output [31:0] out_3,
  output count_out
);

  wire count_8bit_1_count_out, count_8bit_2_count_out, count_8bit_3_count_out;

  count_8bit count_8bit_1 (.clk(clk), .R(R), .value(out_3[7:0]), .count_out(count_8bit_1_count_out));
  count_8bit count_8bit_2 (
    .clk(count_8bit_1_count_out), .R(R), .value(out_3[15:8]), .count_out(count_8bit_2_count_out));
  count_8bit count_8bit_3 (
    .clk(count_8bit_2_count_out), .R(R), .value(out_3[23:16]), .count_out(count_8bit_3_count_out));
  count_8bit count_8bit_4 (.clk(count_8bit_3_count_out), .R(R), .value(out_3[31:24]), .count_out(count_out));
endmodule

module equals (
  input  [31:0] A,
  input  [31:0] B,
  output v_out
);

  wire [31:0] xor_1_out;

  assign xor_1_out = A ^ B;  // XOR_Gate xor_1, 32 bits wide
  nor nor_1 (v_out, xor_1_out[0], xor_1_out[1], xor_1_out[2], xor_1_out[3], xor_1_out[4], xor_1_out[5], xor_1_out[6], xor_1_out[7], xor_1_out[8], xor_1_out[9], xor_1_out[10], xor_1_out[11], xor_1_out[12], xor_1_out[13], xor_1_out[14], xor_1_out[15], xor_1_out[17], xor_1_out[18], xor_1_out[19], xor_1_out[20], xor_1_out[21], xor_1_out[22], xor_1_out[23], xor_1_out[24], xor_1_out[25], xor_1_out[26], xor_1_out[27], xor_1_out[28], xor_1_out[29], xor_1_out[30], xor_1_out[31], xor_1_out[16]);
endmodule
